// Logisim project data3.circ as structural Verilog: 3 circuits, main circuit ★一位全加器FA封装1
// FA
module \一位全加器FA封装1  (
  input  Cin,
  input  Xi,
  input  Yi,
  output Cout,
  output Si
);

  wire AND_2_out, AND_out, XOR_2_out;

  or OR (Cout, AND_out, AND_2_out);
  and AND (AND_out, Xi, Yi);
  and AND_2 (AND_2_out, Cin, XOR_2_out);
  xor XOR (Si, Cin, XOR_2_out);
  xor XOR_2 (XOR_2_out, Xi, Yi);

  // Notes on the sheet:
  //   Si = Xi ^ Yi ^ Cin
  //   Cout = Xi Yi + Cin (Xi ^ Yi)
endmodule

// ADD
module \_8位串行加法器  (
  input  [7:0] X,
  input  [7:0] Y,
  input  Cin,
  output [7:0] S,
  output Cout,
  output Overflow
);

  wire \一位全加器fa封装1_2_cout , \一位全加器fa封装1_3_cout , \一位全加器fa封装1_4_cout , \一位全加器fa封装1_5_cout ,
       \一位全加器fa封装1_6_cout , \一位全加器fa封装1_7_cout , \一位全加器fa封装1_8_cout ;

  xor xor_1 (Overflow, Cout, \一位全加器fa封装1_2_cout );
  \一位全加器FA封装1  \u_一位全加器fa封装1_1  (.Cout(Cout), .Si(S[7]), .Cin(\一位全加器fa封装1_2_cout ), .Xi(X[7]), .Yi(Y[7]));
  \一位全加器FA封装1  \u_一位全加器fa封装1_2  (
    .Cout(\一位全加器fa封装1_2_cout ), .Si(S[6]), .Cin(\一位全加器fa封装1_3_cout ), .Xi(X[6]), .Yi(Y[6]));
  \一位全加器FA封装1  \u_一位全加器fa封装1_3  (
    .Cout(\一位全加器fa封装1_3_cout ), .Si(S[5]), .Cin(\一位全加器fa封装1_4_cout ), .Xi(X[5]), .Yi(Y[5]));
  \一位全加器FA封装1  \u_一位全加器fa封装1_4  (
    .Cout(\一位全加器fa封装1_4_cout ), .Si(S[4]), .Cin(\一位全加器fa封装1_5_cout ), .Xi(X[4]), .Yi(Y[4]));
  \一位全加器FA封装1  \u_一位全加器fa封装1_5  (
    .Cout(\一位全加器fa封装1_5_cout ), .Si(S[3]), .Cin(\一位全加器fa封装1_6_cout ), .Xi(X[3]), .Yi(Y[3]));
  \一位全加器FA封装1  \u_一位全加器fa封装1_6  (
    .Cout(\一位全加器fa封装1_6_cout ), .Si(S[2]), .Cin(\一位全加器fa封装1_7_cout ), .Xi(X[2]), .Yi(Y[2]));
  // Probe on X
  // Probe on Y
  // Probe on S
  \一位全加器FA封装1  \u_一位全加器fa封装1_7  (
    .Cout(\一位全加器fa封装1_7_cout ), .Si(S[1]), .Cin(\一位全加器fa封装1_8_cout ), .Xi(X[1]), .Yi(Y[1]));
  // Probe on X
  // Probe on Y
  // Probe on S
  \一位全加器FA封装1  \u_一位全加器fa封装1_8  (.Cout(\一位全加器fa封装1_8_cout ), .Si(S[0]), .Cin(Cin), .Xi(X[0]), .Yi(Y[0]));

  // Other names for the same wires on the sheet: OF = Overflow

  // Notes on the sheet:
  //   输入引脚区
  //   符号位
  //   输出引脚区
  //   +
  //   =
  //   有符号加法
  //   +
  //   =
  //   无符号加法
endmodule

module \补码一位乘法器  (
  input  [7:0] X,
  input  [7:0] Y,
  output [15:0] \乘积 
);

  wire and_1_out, Ckt, clk, counter_1_carry, sel, xor_1_out, yn, yn_1;
  wire [7:0] multiplexer_1_out, \n8位串行加法器_1_s , not_1_out, Ps, Yt;
  wire [15:1] \部分积 ;

  \_8位串行加法器  \u_8位串行加法器_1  (
    .X(Ps), .Y(multiplexer_1_out), .Cin(and_1_out), .S(\n8位串行加法器_1_s ));  // open: Cout, Overflow
  Register register (.D(\n8位串行加法器_1_s ), .en(Ckt), .Q(\部分积 [15:8]), .clk(clk), .clr(1'b0));
  Multiplexer #(.select(2), .width(8)) multiplexer_1 (
    .in0({8{1'b0}}), .in1(X), .in2(not_1_out), .in3({8{1'b0}}), .out(multiplexer_1_out), .sel({yn, yn_1}),
    .en(1'b1));
  assign not_1_out = ~X;  // NOT_Gate not_1, 8 bits wide
  // Probe on X
  // Probe on \部分积 [15:8]
  and and_1 (and_1_out, yn, xor_1_out);
  xor xor_1 (xor_1_out, yn, yn_1);
  // Probe on Y
  // Probe on {\部分积 [7:1], yn}
  Register Y_2 (.D(Yt), .en(Ckt), .Q({\部分积 [7:1], yn}), .clk(clk), .clr(1'b0));
  Clock clock_1 (.out(clk));
  // Probe on \乘积 
  // Probe on yn_1
  Register #(.width(1)) Yn_1_2 (.D(yn), .en(Ckt), .Q(yn_1), .clk(clk), .clr(1'b0));
  Counter #(.max('h9), .ongoal("stay")) counter_1 (
    .load(1'b0), .count(1'b1), .carry(counter_1_carry), .clk(clk), .clr(1'b0));  // open: D, Q
  Shifter #(.width(16), .shift("ar")) shifter_1 (.in({\部分积 , yn}), .\dist (4'b0001), .out(\乘积 ));
  not not_2 (Ckt, counter_1_carry);
  Register #(.width(1), .trigger("falling")) register_2 (.D(1'b1), .en(1'b1), .Q(sel), .clk(clk), .clr(1'b0));
  Multiplexer #(.width(8), .enable("false")) multiplexer_2 (.in0({8{1'b0}}), .in1(\乘积 [15:8]), .out(Ps), .sel(sel));
  Multiplexer #(.width(8), .enable("false")) multiplexer_3 (.in0(Y), .in1(\乘积 [7:0]), .out(Yt), .sel(sel));

  // Other names for the same wires on the sheet: 部分积[0] = yn
endmodule
